# Fritzing sketch DHT11 (saved by Fritzing 0.9.3b)

parts:
  U1 = ESP32-38PinWide [part_number=ESP32-38PinWide]
  M1 = DHT11-Grove-Temperature-Sensor_1

nets:
  N1: U1.GPIO9, M1.connector0, M1.connector1
  N2: U1.GPIO11, M1.connector3
  N3: U1.VIN, M1.connector2

custom parts:
  ESP32-38PinWide: Generic 38-Pin ESP32 with wide format (only access to one side of pins on a breadboard) based on Stephen Lilley's HiLetgo ESP-WROOM-32 ESP32 ESP-32S Development Board.

// code stored in the sketch: DHT11.ino
#include "DHT.h"	//Librer?a del sensor

#define DHTPIN 9     	// Pin donde est? conectado el sensor
#define DHTTYPE DHT11   //Sensor de temperatura y humedad que se usar?

DHT dht(DHTPIN, DHTTYPE);

void setup() {
  Serial.begin(9600);
  Serial.println("Iniciando...");
  dht.begin();
}

void loop() {
  delay(2000);
  float h = dht.readHumidity(); //Leemos la Humedad
  float t = dht.readTemperature(); //Leemos la temperatura en grados Celsius
  float f = dht.readTemperature(true); //Leemos la temperatura en grados Fahrenheit
  //--------Enviamos las lecturas por el puerto serial-------------
  Serial.print("Humedad ");
  Serial.print(h);
  Serial.println(" %");
  Serial.print("Temperatura: ");
  Serial.print(t);
  Serial.print(" *C y ");
  Serial.print(f);
  Serial.println(" *F");
}
