# Fritzing sketch Laser Emit (saved by Fritzing 0.9.3b)

parts:
  U1 = ESP32-38PinWide [part_number=ESP32-38PinWide]
  Mod1 = KY-008 Laser Transmitter Module [package="Breakout board"]

nets:
  N1: U1.GND, Mod1.-
  N2: U1.GPIO9, Mod1.S
  N3: U1.VIN, Mod1.NC

custom parts:
  ESP32-38PinWide: Generic 38-Pin ESP32 with wide format (only access to one side of pins on a breadboard) based on Stephen Lilley's HiLetgo ESP-WROOM-32 ESP32 ESP-32S Development Board.
  KY-008 Laser Transmitter Module: KY-008 Laser Transmitter Module, emits a dot shaped red laser beam.

// code stored in the sketch: Laser.ino
const int pin = 9; //conectado al pin 9

void setup() {
  pinMode(pin, OUTPUT);  //definir pin como salida
  Serial.begin(9600);    //iniciar la comunicación serial en el puerto 9600
}
 
void loop(){
  digitalWrite(pin, HIGH);   // poner el Pin en HIGH
  Serial.println("Laser encendido");
  delay(5000);               // esperar 5 segundos
  digitalWrite(pin, LOW);    // poner el Pin en LOW
  Serial.println("Laser apagado");
  delay(3000);               // esperar 20 segundos
}
