# Fritzing sketch Big Sound (saved by Fritzing 0.9.3b)

parts:
  U1 = ESP32-38PinWide [part_number=ESP32-38PinWide]
  FC-1 = Sound Sensor

nets:
  N1: U1.GPIO27, FC-1.OUT
  GND: U1.GND, FC-1.GND
  VIN: U1.VIN, FC-1.VCC

custom parts:
  ESP32-38PinWide: Generic 38-Pin ESP32 with wide format (only access to one side of pins on a breadboard) based on Stephen Lilley's HiLetgo ESP-WROOM-32 ESP32 ESP-32S Development Board.

// code stored in the sketch: Big Sound.ino
const int pinMicrophone = 27;

void setup()
{
  Serial.begin(9600);
  pinMode(pinMicrophone, INPUT_PULLUP);
}

void loop()
{
  bool soundDetected = digitalRead(pinMicrophone); //Realiza la lectura del sensor
  if (soundDetected == true)
  {
    Serial.println("Se detecta sonido");
  }else{
    Serial.println("No se detecta sonido");
  }
  delay (1000); //Espera 1 segundo
}
