# Fritzing sketch SMD RGB (saved by Fritzing 0.9.3b)

parts:
  U1 = ESP32-38PinWide [part_number=ESP32-38PinWide]
  Mod1 = KY-009 Full Color RGB LED SMD Module [package="Breakout board"]

nets:
  N1: U1.GPIO19, Mod1.B
  N2: U1.GPIO21, Mod1.G
  N3: U1.GPIO22, Mod1.R
  N4: U1.GND, Mod1.-

custom parts:
  ESP32-38PinWide: Generic 38-Pin ESP32 with wide format (only access to one side of pins on a breadboard) based on Stephen Lilley's HiLetgo ESP-WROOM-32 ESP32 ESP-32S Development Board.
  KY-009 Full Color RGB LED SMD Module: KY-009 RGB full color LED Module, emits a range of colors by mixing red, green and blue light. The amount of each color is adjusted using PWM.

// code stored in the sketch: SMD RGB.ino
//Pines para dar salida a los colores RGB
#define RED 22
#define GRN 21
#define BLU 19
 
void setup() {
   pinMode(RED, OUTPUT);
   pinMode(GRN, OUTPUT);
   pinMode(BLU, OUTPUT);
}
 
void loop() {
   // Encender el LED de color rojo
   digitalWrite(RED, HIGH);
   digitalWrite(GRN, LOW);
   digitalWrite(BLU, LOW);
   delay(1000);
 
   // Encender el LED de color verde
   digitalWrite(RED, LOW);
   digitalWrite(GRN, HIGH);
   digitalWrite(BLU, LOW);
   delay(1000);
 
   // Encender el LED de color azul
   digitalWrite(RED, LOW);
   digitalWrite(GRN, LOW);
   digitalWrite(BLU, HIGH);
   delay(1000);
}
