# Fritzing sketch Hall Magnetic (saved by Fritzing 0.9.3b)

parts:
  U1 = ESP32-38PinWide [part_number=ESP32-38PinWide]
  Mod1 = KY-003 Hall Magnetic Sensor Module [package="Breakout board"]
  LED1 = LED - 5mm [color="Red (633nm)" package="5 mm [THT]"]

nets:
  N1: U1.GPIO14, Mod1.S
  N2: U1.GND, Mod1.-, LED1.cathode
  VIN: U1.VIN, Mod1.Vin
  N3: U1.GPIO23, LED1.anode

custom parts:
  ESP32-38PinWide: Generic 38-Pin ESP32 with wide format (only access to one side of pins on a breadboard) based on Stephen Lilley's HiLetgo ESP-WROOM-32 ESP32 ESP-32S Development Board.
  KY-003 Hall Magnetic Sensor Module: KEYES KY-003 Arduino Hall Magnetic Sensor Module is a switch that will turn on/off in the presence of a magnetic field.

// code stored in the sketch: Hall Magnetic.ino
const int HALLPin = 14;
const int LEDPin = 23;

void setup() {
  Serial.begin(9600);
  pinMode(LEDPin, OUTPUT);
  pinMode(HALLPin, INPUT);
}

void loop() {
  if(digitalRead(HALLPin)==HIGH){ //Realizar la lectura del pin
    Serial.println("Se detecta campo electromagnético");
    digitalWrite(LEDPin, HIGH);
  }
  else{
    Serial.println("No se está detectando ningún campo electromagnético");
    digitalWrite(LEDPin, LOW);
  }
}
