# Fritzing sketch Linear Hall (saved by Fritzing 0.9.3b)

parts:
  U1 = ESP32-38PinWide [part_number=ESP32-38PinWide]
  Mod1 = KY-024 Linear Hall Magnetic Sensor Module [package="Breakout board"]

nets:
  N1: U1.GPIO39, Mod1.A0
  N2: U1.GPIO25, Mod1.D0
  N3: U1.GND, Mod1.G
  N4: U1.VIN, Mod1.+

custom parts:
  ESP32-38PinWide: Generic 38-Pin ESP32 with wide format (only access to one side of pins on a breadboard) based on Stephen Lilley's HiLetgo ESP-WROOM-32 ESP32 ESP-32S Development Board.
  KY-024 Linear Hall Magnetic Sensor Module: KY-024 Linear Hall Magnetic Sensor Module reacts iin the presence of a magnetic field.

// code stored in the sketch: Linear Hall.ino
//initiation des pins
int digitalPin = 25; //pin Digital
int analogPin = 39; //pin Analógico
int digitalVal;
int analogVal;

void setup()
{
 	Serial.begin(9600); // Inicia la comunicación serial
 	pinMode(digitalPin, INPUT); //Se defiune el pin digital como uno de entrada
}
void loop()
{
 	digitalVal = digitalRead(digitalPin); //Lectura del pin
 	if (digitalVal == HIGH){
 			Serial.println("Se detecta un campo magnético");
 	}
 	else{
 			Serial.println("No se está detectando nada");
 	}
 	analogVal = analogRead(analogPin);
 	Serial.println(analogVal); //Se imprime el valor del pin analógico
 	delay(500); //Espera 500 milisegundos
}
