# Fritzing sketch Sensor de Gas MQ-2 (saved by Fritzing 0.9.3b)

parts:
  U1 = ESP32-38PinWide [part_number=ESP32-38PinWide]
  Componente1 = MQ-3 breakout

nets:
  VIN: U1.VIN, Componente1.VCC
  N1: U1.GPIO6, Componente1.DO
  GND: U1.GND, Componente1.GND

custom parts:
  ESP32-38PinWide: Generic 38-Pin ESP32 with wide format (only access to one side of pins on a breadboard) based on Stephen Lilley's HiLetgo ESP-WROOM-32 ESP32 ESP-32S Development Board.
  MQ-3 breakout: Alcohol sensor is capable of detecting alcohol (ethanol) particles on itself and gives the information in digital form back to us to manipulate with it. SKU:101251 • Voltage: 5V DC • Power: max 750mW • Measurement range: 0.04-4mg/L

// code stored in the sketch: Sensor de Gas MQ-2.ino
int pin_mq = 6; //Pin digital para el sensor de gas
void setup() { 
  Serial.begin(9600);
  pinMode(pin_mq, INPUT);
}


void loop() {
  
  boolean mq_estado = digitalRead(pin_mq);//Leemos el sensor
  if(mq_estado) //Si la salida del sensor es 1
  {
    Serial.println("Sin presencia de gas o humo");
  }
  else //Si la salida del sensor es 0
  {
    Serial.println("Humo o gas detectado");
  }
  delay(500); //Espera 500 milisegundos
}
