# Fritzing sketch Avoid - Motor de Corriente Continua (saved by Fritzing 0.9.3b)

parts:
  U1 = ESP32-38PinWide [part_number=ESP32-38PinWide]
  S1 = H-Bridge with L298N
  Mod1 = KY-032 IR Obstacle Avoidance Sensor Module [package="Breakout board"]
  M1 = DC Motor

nets:
  N1: U1.3.3, Mod1.+
  N2: U1.GPIO34, S1.IN4
  N3: U1.GPIO35, S1.IN3
  GND: U1.GND, S1.GND, Mod1.GND
  VIN: U1.VIN, S1.12V
  N4: U1.GPIO22, Mod1.out
  N5: S1.M1-02, S1.M2-01, S1.M2-02, S1.ENA-5V, S1.ENB-5V, M1.pin_1, M1.pin_2

custom parts:
  ESP32-38PinWide: Generic 38-Pin ESP32 with wide format (only access to one side of pins on a breadboard) based on Stephen Lilley's HiLetgo ESP-WROOM-32 ESP32 ESP-32S Development Board.
  H-Bridge with L298N: h-bridge
  KY-032 IR Obstacle Avoidance Sensor Module: KY-032 Infrared Obstacle Avoidance Sensor. Distance-adjustable, infrared proximity sensor designed for wheeled robots. Also known as AD-032.

// code stored in the sketch: Avoid - Motor de Corriente Continua.ino
int IN3 = 35; 
int IN4 = 34;
int SensorPin = 22;
int avoid;

void setup(){
  pinMode (IN4, OUTPUT);    // Input4 conectada al pin 4 
  pinMode (IN3, OUTPUT);    // Input3 conectada al pin 5
  pinMode(SensorPin, INPUT);
  Serial.begin(9600);
}
void loop(){
  avoid = digitalRead(SensorPin);
  if(avoid == HIGH){
    // Motor gira en un sentido
    digitalWrite (IN4, HIGH);
    digitalWrite (IN3, LOW);
    Serial.println("Se detecta un obstáculo");
    delay(3000);
  }else{
    // Motor no gira
    digitalWrite (IN4, LOW);
    Serial.println("No hay obstáculos");
  }
}
