# Fritzing sketch Sensor Temp LM35 - Servo motor (saved by Fritzing 0.9.3b)

parts:
  U1 = ESP32-38PinWide [part_number=ESP32-38PinWide]
  J1 = Basic Servo
  T1 = LM35 Temperature Sensor [package="TO92 [THT]"]

nets:
  N1: U1.3.3, T1.+Vs
  N2: U1.GPIO39, T1.Vout
  N3: U1.GPIO27, J1.pulse
  GND: U1.GND, J1.gnd, T1.GND
  VIN: U1.VIN, J1.vcc

custom parts:
  ESP32-38PinWide: Generic 38-Pin ESP32 with wide format (only access to one side of pins on a breadboard) based on Stephen Lilley's HiLetgo ESP-WROOM-32 ESP32 ESP-32S Development Board.

// code stored in the sketch: Sensor Temp LM35 - Servo motor.ino
// Incluímos la librería para poder controlar el servo
#include <Servo.h>

// Declaramos la variable para controlar el servo
Servo servoMotor;

// Variable para el pin del sensor
const int SensorPin = 39;

void setup() {
  // Iniciamos el monitor serie para mostrar el resultado
  Serial.begin(9600);
  // Iniciamos el servo para que empiece a trabajar con el pin 27
  servoMotor.attach(27);
  // Se define el pin del sensor como entrada
  pinMode(SensorPin, INPUT);
}

void loop() {
  int value = analogRead(SensorPin);
  Serial.println(value);
  delay(1000);
  if(value > 20){
    servoMotor.write(90);
    delay(1000);
    servoMotor.write(180);
    delay(1000);
  }else{
    servoMotor.write(0);
  }
}
