# Fritzing sketch Knock Sensor Module - Stepper Motor (saved by Fritzing 0.9.3b)

parts:
  Driver1 = 28BYJ-48 Driver Module [part_number=ULN2003 package=THT]
  SM1 = 28BYJ-48 Stepper Motor [part_number=28BYJ-48]
  U1 = ESP32-38PinWide [part_number=ESP32-38PinWide]
  Mod1 = KY-031 Knock Sensor Module [package="Breakout board"]

nets:
  N1: Driver1.IN1, U1.GPIO18
  N2: Driver1.IN2, U1.GPIO5
  N3: Driver1.IN3, U1.GPIO17
  N4: Driver1.IN4, U1.GPIO16
  N5: Driver1.blue-pin, SM1.blue-pin
  N6: Driver1.pink-pin, SM1.pink-pin
  N7: Driver1.yellow-pin, SM1.yellow-pin
  N8: Driver1.orange-pin, SM1.orange-pin
  N9: Driver1.red-pin, SM1.red-pin
  N10: U1.GPIO12, Mod1.S
  N11: U1.GND, Mod1.-
  VIN: U1.VIN, Mod1.Vin

custom parts:
  28BYJ-48 Driver Module: Generic male header
  28BYJ-48 Stepper Motor: Unipolar Stepper Motor 28BYJ-48 Top coil - pink & orange Bottom coil - blue & yellow Common rail - red Connector pins: blue - pink - yellow - orange - red
  ESP32-38PinWide: Generic 38-Pin ESP32 with wide format (only access to one side of pins on a breadboard) based on Stephen Lilley's HiLetgo ESP-WROOM-32 ESP32 ESP-32S Development Board.
  KY-031 Knock Sensor Module: KY-031 Knock Sensor module. A vibration sensor that sends a signal when a knock/tap is detected.

// code stored in the sketch: Knock Sensor Module - Stepper Motor.ino
#include <Stepper.h>

int Shock = 12;
int val;
double stepsPerRevolution = 2048;
Stepper myStepper(stepsPerRevolution, 18, 5, 17, 16);  // Pin inversion to make the library work

void setup() {
  pinMode (Shock, INPUT);
  myStepper.setSpeed(10);
  Serial.begin(9600);
}

void loop(){
  val = digitalRead (Shock);
  if (val == HIGH) {
  Serial.println("Detecta un golpe");
  myStepper.step(stepsPerRevolution);
  }else{
  Serial.println("No detecta un golpe");
  myStepper.step(-stepsPerRevolution);
  }
}
