# Fritzing sketch Sensor ultrasonico - Display de 7 segmentos (saved by Fritzing 0.9.3b)

parts:
  Grove1 = Grove 4 Digit Display
  U1 = ESP32-38PinWide [part_number=ESP32-38PinWide]
  Componente1 = HC-SR04

nets:
  GND: Grove1.GND, U1.GND, Componente1.Gnd
  VCC: Grove1.VCC, U1.VIN
  N1: Grove1.DIO, U1.GPIO27
  N2: Grove1.CLK, U1.GPIO26
  N3: U1.3.3, Componente1.Vcc
  N4: U1.GPIO21, Componente1.Trig
  N5: U1.GPIO1, Componente1.Echo

custom parts:
  ESP32-38PinWide: Generic 38-Pin ESP32 with wide format (only access to one side of pins on a breadboard) based on Stephen Lilley's HiLetgo ESP-WROOM-32 ESP32 ESP-32S Development Board.
  HC-SR04: HC-SR04 ultrasonic distance sensor

// code stored in the sketch: Sensor ultrasonico - Display de 7 segmentos.ino
#include <TM1637Display.h>

// Pines de conexión de la pantalla
const int CLK = 26;
const int DIO = 27;
// Pines de conexión del sensor
const int Trigger = 21;
const int Echo = 1;

// Creamos una instancia de la clase TM1637Display y la llamamos "display"
TM1637Display display(CLK, DIO);

// Codificación de una línea horizontal
const uint8_t linea[] = {
  SEG_G, SEG_G, SEG_G, SEG_G
};

void setup() {
  display.setBrightness(5);// Indicamos el brillo de los segmentos (0 = mínimo; 7 = máximo)
  Serial.begin(9600);//iniciailzamos la comunicación
  pinMode(Trigger, OUTPUT); //pin como salida
  pinMode(Echo, INPUT);  //pin como entrada
  digitalWrite(Trigger, LOW);//Inicializamos el pin con 0  
}

void loop() {
  long t; //timepo que demora en llegar el eco
  long d; //distancia en centimetros

  digitalWrite(Trigger, HIGH);
  delayMicroseconds(10);          //Enviamos un pulso de 10us
  digitalWrite(Trigger, LOW);
  
  t = pulseIn(Echo, HIGH); //obtenemos el ancho del pulso
  d = t/59;             //escalamos el tiempo a una distancia en cm
  
  display.showNumberDec(d); // Se imprime la distancia en centímetros en el display
  delay(1000); // Espera un segundo

  display.setSegments(linea); // Imprime una ínea horizontal
  delay(1000); // Espera un segundo
}
