# Fritzing sketch Rotary encoders - Display TFT (saved by Fritzing 0.9.3b)

parts:
  U1 = ESP32-38PinWide [part_number=ESP32-38PinWide]
  RE1 = KY-040 Rotary encoder [package=THT]
  TFT1 = 1.44" SPI TFT Graphics Display 128x128 [package=THT]

nets:
  N1: U1.GPIO33, TFT1.pin4
  N2: U1.GPIO14, TFT1.pin9
  GND: U1.GND, RE1.GND, TFT1.pin2, TFT1.pin3
  N3: U1.GPIO9, TFT1.pin10
  N4: U1.GPIO10, TFT1.pin11
  VIN: U1.VIN, RE1.Vcc, TFT1.pin1
  N5: U1.GPIO7, RE1.SW
  N6: U1.GPIO8, RE1.DT
  N7: U1.GPIO15, RE1.CLK

custom parts:
  ESP32-38PinWide: Generic 38-Pin ESP32 with wide format (only access to one side of pins on a breadboard) based on Stephen Lilley's HiLetgo ESP-WROOM-32 ESP32 ESP-32S Development Board.
  KY-040 Rotary encoder: KY-040 Rotary Encoder with switch on breakout borad from AZ Delivery
  1.44" SPI TFT Graphics Display 128x128: This is for https://www.amazon.com/gp/product/B07B4BDWCL/ref=ask_ql_qh_dp_hza display. Note that this display is sold with a misprinted silkscreen indicating I2C connections on P2 connector, it is actualy SPI. The P1 connections are non functional on this board from the linked URL seller on Amazon.

// code stored in the sketch: Rotary encoders - Display TFT.ino
#include <Adafruit_GFX.h>    // Core graphics library
#include <Adafruit_ST7735.h> // Hardware-specific library for ST7735
#include <Adafruit_ST7789.h> // Hardware-specific library for ST7789
#include <SPI.h>

const int clkPin 	= 15;
const int dtPin 	= 8;
const int swPin 	= 7;

int rotVal 	= 0;
bool clkState 	= LOW;
bool clkLast 	= HIGH;
bool swState 	= HIGH;
bool swLast 	= HIGH;

#if defined(ARDUINO_FEATHER_ESP32) // Feather Huzzah32
  #define TFT_CS         14
  #define TFT_RST        15
  #define TFT_DC         32

#elif defined(ESP8266)
  #define TFT_CS         4
  #define TFT_RST        16                                            
  #define TFT_DC         5

#else
  // For the breakout board, you can use any 2 or 3 pins.
  // These pins will also work for the 1.8" TFT shield.
  #define TFT_CS        10
  #define TFT_RST        8 // Or set to -1 and connect to Arduino RESET pin
  #define TFT_DC         14
#endif

// For 1.44" and 1.8" TFT with ST7735 use:
Adafruit_ST7735 tft = Adafruit_ST7735(TFT_CS, TFT_DC, TFT_RST);

void setup(void) {
  Serial.begin(9600);

  tft.initR(INITR_BLACKTAB);      // Init ST7735S chip, black tab
  tft.initR(INITR_MINI160x80);  // Init ST7735S mini display
  pinMode(clkPin,INPUT);
 	pinMode(dtPin,INPUT);
 	pinMode(swPin,INPUT_PULLUP); 
  
  // large block of text
  tft.fillScreen(ST77XX_BLACK);  
}

void loop() {
   tft.setCursor(0, 0);
   tft.print("Oscar Adahir Rojas Sánchez");
  clkState = digitalRead(clkPin);
 	if ((clkLast == LOW) && (clkState == HIGH)) {//rotary moving
 			Serial.print("Rotary position ");
 			if (digitalRead(dtPin) == HIGH) {
 					rotVal = rotVal - 1;
 					if ( rotVal < 0 ) {
 							rotVal = 0;
 					}
 			}
 			else {
 					rotVal++;
 					if ( rotVal > 10 ) {
 							rotVal = 10;
 					}
 			} 
      Serial.println(rotVal);
      char val[10];
      dtostrf(rotVal,5,0,val);
      tft.setCursor(0, 20);
      tft.print("El valor es ");
      tft.print(val);
      delay(1000);
      tft.fillScreen(ST77XX_BLACK);
 	}
 	clkLast = clkState;

}
