# Fritzing sketch Photo Interruptor - Display de matriz LED (saved by Fritzing 0.9.3b)

parts:
  U1 = ESP32-38PinWide [part_number=ESP32-38PinWide]
  Componente1 = LED Matrix - Serial Interface - Red/Green/Blue
  Componente2 = LED Matrix - Serial Interface - Red/Green/Blue  # not connected
  Componente3 = LED Matrix - Serial Interface - Red/Green/Blue  # not connected
  Componente4 = LED Matrix - Serial Interface - Red/Green/Blue  # not connected
  Mod1 = KY-010 Photo Interrupter Module [package="Breakout board"]

nets:
  N1: U1.3.3, Mod1.Vin
  N2: U1.GPIO27, Componente1.CS
  N3: U1.GPIO14, Componente1.SCK
  GND: U1.GND, Componente1.GND, Mod1.-
  VIN: U1.VIN, Componente1.VCC
  N4: U1.GPIO15, Componente1.MISO
  N5: U1.GPIO5, Mod1.S

custom parts:
  ESP32-38PinWide: Generic 38-Pin ESP32 with wide format (only access to one side of pins on a breadboard) based on Stephen Lilley's HiLetgo ESP-WROOM-32 ESP32 ESP-32S Development Board.
  KY-010 Photo Interrupter Module: KY-010 Photo Interrupter Module, it will trigger a signal when light between the sensor's gap is blocked.

// code stored in the sketch: Photo Interruptor - Display de matriz LED.ino
#include <Adafruit_GFX.h>
#include <Adafruit_NeoMatrix.h>
#include <Adafruit_NeoPixel.h>
#ifndef PSTR
#define PSTR // Make Arduino Due happy
#endif

#define PIN 14
int sensr = 5;
int val;
String res;

// Forma en la que se va a imprimir el valor
Adafruit_NeoMatrix matrix = Adafruit_NeoMatrix(8, 8, 4, 1, PIN,
  NEO_TILE_TOP   + NEO_TILE_LEFT   + NEO_TILE_COLUMNS   + NEO_TILE_PROGRESSIVE +
  NEO_MATRIX_TOP + NEO_MATRIX_LEFT + NEO_MATRIX_COLUMNS + NEO_MATRIX_ZIGZAG,
  NEO_GRB + NEO_KHZ800);

const uint16_t colors[] = {
  matrix.Color(255, 0, 0), matrix.Color(0, 255, 0), matrix.Color(0, 0, 255) };

void setup() {
  matrix.begin();
  matrix.setTextWrap(false);
  matrix.setBrightness(40);
  matrix.setTextColor(colors[0]);
  pinMode (sensr, INPUT);
  Serial.begin(9600);
}

int x    = matrix.width();
int pass = 0;

void loop() {
  // Se lee el sensor y de acuerdo al valor se muestra un mensaje en la matríz
  val = digitalRead (sensr);
  if (val == HIGH) {
    res = "Apagado";
  }else{
    res = "Encendido";
  }
  String imp = "Oscar Rojas "+res;
  Serial.println(imp);
  
  // Mover el mensaje por la matríz
  matrix.fillScreen(0);
  matrix.setCursor(x, 0);
  matrix.print(imp);
  if(--x < -150) {
    x = matrix.width();
    if(++pass >= 3) pass = 0;
    matrix.setTextColor(colors[pass]);
  }
  matrix.show();
  delay(100);
}
